// Logisim project Control-unit.circ as structural Verilog: 1 circuit, main circuit main
module main (
  input  [2:0] OPCode,
  output RegDst,
  output RegWrite,
  output ALU_SRC,
  output Mem_Read,
  output Mem_Write,
  output MemToReg,
  output Brance,
  output Jump,
  output [1:0] ALUop
);

  and R_type (ALUop[0], ~OPCode[0], ~OPCode[1], ~OPCode[2]);  // AND_Gate
  and LW (Mem_Read, ~OPCode[0], ~OPCode[1], OPCode[2]);  // AND_Gate
  and SW (Mem_Write, ~OPCode[0], OPCode[1], ~OPCode[2]);  // AND_Gate
  and Beq (ALUop[1], ~OPCode[0], OPCode[1], OPCode[2]);  // AND_Gate
  and u_Jump (Jump, OPCode[0], ~OPCode[1], ~OPCode[2]);  // AND_Gate
  or or_1 (RegWrite, ALUop[0], Mem_Read);
  or or_2 (ALU_SRC, Mem_Read, Mem_Write);

  assign Brance = ALUop[1];
  assign MemToReg = Mem_Read;
  assign RegDst = ALUop[0];
endmodule
