// Logisim project lubba-CPU-16-bit.circ as structural Verilog: 1 circuit, main circuit main
module main (
  input  Cin,
  output out_2,
  output [15:0] out_3,
  output [15:0] out_4,
  output [3:0] out_5
);

  wire and_1_out, CLK_out, control_unit_1_p2, control_unit_1_p3, control_unit_1_p4, control_unit_1_p5,
       control_unit_1_p6, control_unit_1_p7, control_unit_1_p8, control_unit_1_p9, control_unit_1_p10;
  wire [2:0] control_unit_1_p12;
  wire [15:0] adder_1_out, adder_2_out, bit_extender_1_out, jump_1_p3, multiplexer_2_out, multiplexer_3_out,
       multiplexer_4_out, n16_bit_alu_1_result, PC_q, ram_1_data, register_file_1_p3, rom_1_data;

  Register #(.width(16)) PC (.D(multiplexer_4_out), .Q(PC_q), .clk(CLK_out));  // open: en, clr
  Clock CLK (.out(CLK_out));
  Adder #(.width(16)) adder_1 (.a(PC_q), .b(16'h1), .out(adder_1_out), .cin(Cin));  // open: cout
  ROM #(.addrWidth(16), .dataWidth(16)) rom_1 (.addr(PC_q), .data(rom_1_data));  // open: sel
  // jump jump_1: pin names not known; wires that end beside it: adder_1_out, rom_1_data, jump_1_p3, out_4
  // control_unit control_unit_1: pin names not known; wires that end beside it: rom_1_data[15:13], control_unit_1_p2, control_unit_1_p3, control_unit_1_p4, control_unit_1_p5, control_unit_1_p6, control_unit_1_p7, control_unit_1_p8, control_unit_1_p9, control_unit_1_p10, rom_1_data[9:7], control_unit_1_p12, CLK_out
  Multiplexer #(.width(3)) multiplexer_1 (
    .in0(rom_1_data[9:7]), .in1(rom_1_data[6:4]), .out(control_unit_1_p12), .sel(control_unit_1_p2));  // open: en
  // register_file register_file_1: pin names not known; wires that end beside it: rom_1_data[12:10], control_unit_1_p3, register_file_1_p3, out_3
  assign bit_extender_1_out = {{9{rom_1_data[6]}}, rom_1_data[6:0]};  // Bit_Extender bit_extender_1
  Multiplexer #(.width(16)) multiplexer_2 (
    .in0(out_3), .in1(bit_extender_1_out), .out(multiplexer_2_out), .sel(control_unit_1_p4));  // open: en
  Adder #(.width(16)) adder_2 (.a(adder_1_out), .b(bit_extender_1_out), .out(adder_2_out));  // open: cin, cout
  and and_1 (and_1_out, control_unit_1_p8, out_2);
  _16_bit_alu u_16_bit_alu_1 (
    .B(multiplexer_2_out), .A(register_file_1_p3), .ALU_Op(out_5[1:0]), .result(n16_bit_alu_1_result),
    .zero(out_2), .B_Inv(out_5[2]), .Cin(out_5[2]));  // open: Overflow
  // ALU_control alu_control_1: pin names not known; wires that end beside it: control_unit_1_p10, rom_1_data[3:0], out_5
  Multiplexer #(.width(16)) multiplexer_3 (
    .in0(adder_1_out), .in1(adder_2_out), .out(multiplexer_3_out), .sel(and_1_out));  // open: en
  Multiplexer #(.width(16)) multiplexer_4 (
    .in0(multiplexer_3_out), .in1(jump_1_p3), .out(multiplexer_4_out), .sel(control_unit_1_p9));  // open: en
  RAM #(.addrWidth(16), .dataWidth(16), .bus("separate")) ram_1 (
    .addr(n16_bit_alu_1_result), .din(out_3), .data(ram_1_data), .str(control_unit_1_p6), .clk(CLK_out),
    .ld(control_unit_1_p5));  // open: sel, clr
  Multiplexer #(.width(16)) multiplexer_5 (
    .in0(n16_bit_alu_1_result), .in1(ram_1_data), .out(out_4), .sel(control_unit_1_p7));  // open: en

  // Notes on the sheet:
  //   funct
  //   opcode
endmodule
